# Fritzing sketch temp-device (saved by Fritzing 1.0.2b)
breadboards: 1

parts:
  Part1 = MCP9808 High Accuracy I2C Temperature Sensor [part_number=1782]
  Mod1 = Raspberry Pi Pico W
  OLED2 = 128x64 Monochrom OLED Display with SPI Control
  S1 = Pushbutton [package="[THT]"]
  S2 = Pushbutton [package="[THT]"]
  LED1 = RGB LED (com. cathode, rbg) [color="Red (633nm)" current=0.030A package="5 mm [THT]"]
  R1 = Resistor [tolerance=±5% resistance=220 package="2512 [SMD]"]
  R2 = Resistor [tolerance=±5% resistance=220 package="2512 [SMD]"]
  R3 = Resistor [tolerance=±5% resistance=220 package="2512 [SMD]"]
  R4 = Resistor [tolerance=±5% resistance=10k package="2512 [SMD]"]
  R5 = Resistor [tolerance=±5% resistance=10k package="2512 [SMD]"]

nets:
  VDD: Part1.VDD, Mod1.pin_36, OLED2.3v3
  GND: Part1.GND, Mod1.pin_1, Mod1.pin_2, Mod1.pin_3, Mod1.pin_8, Mod1.pin_13, Mod1.pin_18, Mod1.pin_23, Mod1.pin_28, Mod1.pin_33, Mod1.pin_38, Mod1.pin_42, OLED2.GND, S1.Pin_1, S1.Pin_2, S1.Pin_3, S1.Pin_4, S2.Pin_1, S2.Pin_2, S2.Pin_3, S2.Pin_4, LED1.blue_anode, R4.Pin_0, R4.Pin_1, R5.Pin_0, R5.Pin_1
  N1: Part1.SCL, Mod1.pin_27
  N2: Part1.SDA, Mod1.pin_26
  N3: Mod1.pin_10, R3.Pin_1
  N4: Mod1.pin_11, R2.Pin_1
  N5: Mod1.pin_12, R1.Pin_1
  N6: Mod1.pin_22, OLED2.CS
  N7: Mod1.pin_24, OLED2.Clock
  N8: Mod1.pin_25, OLED2.Data
  N9: Mod1.pin_29, OLED2.SA0/DC
  N10: Mod1.pin_30, OLED2.Reset
  N11: LED1.red_anode, R3.Pin_0
  N12: LED1.common_cathode, R2.Pin_0
  N13: LED1.green_anode, R1.Pin_0

custom parts:
  MCP9808 High Accuracy I2C Temperature Sensor: This I2C digital temperature sensor is one of the more accurate/precise we've ever seen, with a typical accuracy of ±0.25°C over the sensor's -40°C to +125°C range and precision of +0.0625°C. They work great with any microcontroller using standard i2c. There are 3 address pins so you can connect up to 8 to a single I2C bus without address collisions. Best of all, a wide voltage range makes is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
  Raspberry Pi Pico W: Raspberry Pi Pico W. Based around the RP2040 microcontroller the Pico W is a low cost microcontroller device bringing Raspberry Pi quality, cost, and easy of use to the microcontroller space. The areas marked KEEPOUT in pcb silkscreen should not have traces running through them to avoid shorts on a soldered in module!
